# Fritzing sketch IoT (saved by Fritzing 0.9.3b)
breadboards: 1

parts:
  Componente1 = Arduino Uno (Rev3)
  RHT1 = Humidity and Temperature Sensor RHT03
  IC1 = DS1302 [package="SO8 [SMD]"]
  U1 = 7-SEGMENT-4DIGIT [package=7-segment-4digit]
  GSM_SIM_GPSR_SMS_SIM900_SIM1 = SIM800L [package=THT]
  U2 = SD_CARD_SOCKET [package=sdcard_4uconn]

nets:
  N1: Componente1.A4/SDA, IC1.I/O_-_SPI_Data_In/Out
  N2: Componente1.A5/SCL, IC1.SCLK_-_SPI_Clock
  N3: Componente1.D8, GSM_SIM_GPSR_SMS_SIM900_SIM1.SIM_RXD
  N4: Componente1.D9_PWM, U2.VDD
  N5: Componente1.D10_PWM/SS, U2.VSS1
  N6: Componente1.D11_PWM/MOSI, U2.CMD
  GND: Componente1.D12/MISO, Componente1.GND, RHT1.GND_2, IC1.0V, U1.6, U1.8, GSM_SIM_GPSR_SMS_SIM900_SIM1.GND, U2.SH
  N7: Componente1.D13/SCK, U2.CD_DAT3
  N8: Componente1.D3_PWM, U1.5
  N9: Componente1.D4, U1.3, U1.4
  N10: Componente1.D5_PWM, RHT1.Data-signal
  N11: Componente1.D7, GSM_SIM_GPSR_SMS_SIM900_SIM1.SIM_TXD
  5V: Componente1.5V, RHT1.Vcc, IC1.+V, U1.7, GSM_SIM_GPSR_SMS_SIM900_SIM1.VDD, U2.CLK
